// Logisim project ignition_mealy.circ as structural Verilog: 1 circuit, main circuit main
module main (
  input  start_engine,
  input  engine_running,
  output starter_motor,
  output ignition_coil
);

  wire and_1_out, and_2_out, and_3_out, and_4_out, and_5_out, and_6_out, and_7_out, and_8_out, and_9_out,
       and_10_out, and_11_out, and_12_out, and_13_out, and_14_out, and_15_out, and_16_out, and_17_out,
       clock_1_out, D0, D1, notER, notQ0, notQ1, notSE, Q0, Q1;

  not not_1 (notSE, start_engine);
  not not_2 (notER, engine_running);
  Clock clock_1 (.out(clock_1_out));
  and and_1 (and_1_out, notQ1, notQ0, start_engine);
  and and_2 (and_2_out, Q0, start_engine);
  and and_3 (and_3_out, notQ1, Q0, notER);
  and and_4 (and_4_out, Q1, notQ0, start_engine, engine_running);
  and and_5 (and_5_out, Q1, Q0, notSE, engine_running);
  and and_6 (and_6_out, notQ1, Q0, notSE, engine_running);
  and and_7 (and_7_out, Q1, notQ0, engine_running);
  and and_8 (and_8_out, Q1, Q0, notSE, engine_running);
  and and_9 (and_9_out, Q1, Q0, start_engine);
  D_Flip_Flop d_ff_1 (.D(D0), .clk(clock_1_out), .Q(Q0), .Qn(notQ0));  // open: preset, reset
  D_Flip_Flop d_ff_2 (.D(D1), .clk(clock_1_out), .Q(Q1), .Qn(notQ1));  // open: preset, reset
  or or_1 (D0, and_1_out, and_2_out, and_3_out, and_4_out, and_5_out);
  or or_2 (D1, and_6_out, and_7_out, and_8_out, and_9_out);
  and and_10 (and_10_out, notQ1, notQ0, start_engine);
  and and_11 (and_11_out, notQ1, Q0, start_engine);
  and and_12 (and_12_out, notQ1, Q0, notER);
  and and_13 (and_13_out, notQ1, notQ0, start_engine);
  and and_14 (and_14_out, notQ1, Q0, notSE, engine_running);
  and and_15 (and_15_out, notQ1, Q0, start_engine);
  and and_16 (and_16_out, notQ1, Q0, notER);
  and and_17 (and_17_out, Q1, notQ0, notSE, engine_running);
  or or_3 (starter_motor, and_10_out, and_11_out, and_12_out);
  or or_4 (ignition_coil, and_13_out, and_14_out, and_15_out, and_16_out, and_17_out);

  // Other names for the same wires on the sheet: ER = engine_running; IC = ignition_coil; SE = start_engine;
  //   SM = starter_motor
endmodule
