// Logisim project my_adder.circ as structural Verilog: 2 circuits, main circuit main
module main (
  input  sub,
  input  [15:0] A,
  input  [15:0] B,
  output [15:0] result,
  output ovf
);

  wire Bbit0, Bbit1, Bbit2, Bbit3, Bbit4, Bbit5, Bbit6, Bbit7, Bbit8, Bbit9, Bbit10, Bbit11, Bbit12, Bbit13,
       Bbit14, Bbit15, Cout0, Cout1, Cout2, Cout3, Cout4, Cout5, Cout6, Cout7, Cout8, Cout9, Cout10, Cout11,
       Cout12, Cout13, Cout14, Cout15;

  xor xor_1 (Bbit0, B[0], sub);
  xor xor_2 (Bbit1, B[1], sub);
  xor xor_3 (Bbit2, B[2], sub);
  xor xor_4 (Bbit3, B[3], sub);
  xor xor_5 (Bbit4, B[4], sub);
  xor xor_6 (Bbit5, B[5], sub);
  xor xor_7 (Bbit6, B[6], sub);
  xor xor_8 (Bbit7, B[7], sub);
  xor xor_9 (Bbit8, B[8], sub);
  xor xor_10 (Bbit9, B[9], sub);
  xor xor_11 (Bbit10, B[10], sub);
  xor xor_12 (Bbit11, B[11], sub);
  xor xor_13 (Bbit12, B[12], sub);
  xor xor_14 (Bbit13, B[13], sub);
  xor xor_15 (Bbit14, B[14], sub);
  xor xor_16 (Bbit15, B[15], sub);
  full_adder full_adder_1 (.Cout(Cout0), .sum(result[0]), .Cin(sub), .B(Bbit0), .A(A[0]));
  full_adder full_adder_2 (.Cout(Cout1), .sum(result[1]), .Cin(Cout0), .B(Bbit1), .A(A[1]));
  full_adder full_adder_3 (.Cout(Cout2), .sum(result[2]), .Cin(Cout1), .B(Bbit2), .A(A[2]));
  full_adder full_adder_4 (.Cout(Cout3), .sum(result[3]), .Cin(Cout2), .B(Bbit3), .A(A[3]));
  full_adder full_adder_5 (.Cout(Cout4), .sum(result[4]), .Cin(Cout3), .B(Bbit4), .A(A[4]));
  full_adder full_adder_6 (.Cout(Cout5), .sum(result[5]), .Cin(Cout4), .B(Bbit5), .A(A[5]));
  full_adder full_adder_7 (.Cout(Cout6), .sum(result[6]), .Cin(Cout5), .B(Bbit6), .A(A[6]));
  full_adder full_adder_8 (.Cout(Cout7), .sum(result[7]), .Cin(Cout6), .B(Bbit7), .A(A[7]));
  full_adder full_adder_9 (.Cout(Cout8), .sum(result[8]), .Cin(Cout7), .B(Bbit8), .A(A[8]));
  full_adder full_adder_10 (.Cout(Cout9), .sum(result[9]), .Cin(Cout8), .B(Bbit9), .A(A[9]));
  full_adder full_adder_11 (.Cout(Cout10), .sum(result[10]), .Cin(Cout9), .B(Bbit10), .A(A[10]));
  full_adder full_adder_12 (.Cout(Cout11), .sum(result[11]), .Cin(Cout10), .B(Bbit11), .A(A[11]));
  full_adder full_adder_13 (.Cout(Cout12), .sum(result[12]), .Cin(Cout11), .B(Bbit12), .A(A[12]));
  full_adder full_adder_14 (.Cout(Cout13), .sum(result[13]), .Cin(Cout12), .B(Bbit13), .A(A[13]));
  full_adder full_adder_15 (.Cout(Cout14), .sum(result[14]), .Cin(Cout13), .B(Bbit14), .A(A[14]));
  full_adder full_adder_16 (.Cout(Cout15), .sum(result[15]), .Cin(Cout14), .B(Bbit15), .A(A[15]));
  xor xor_17 (ovf, Cout14, Cout15);

  // Other names for the same wires on the sheet: Abit0 = A[0]; Abit1 = A[1]; Abit2 = A[2]; Abit3 = A[3]; Abit4 = A[4];
  //   Abit5 = A[5]; Abit6 = A[6]; Abit7 = A[7]; Abit8 = A[8]; Abit9 = A[9]; Abit10 = A[10]; Abit11 = A[11];
  //   Abit12 = A[12]; Abit13 = A[13]; Abit14 = A[14]; Abit15 = A[15]; sum0 = result[0]; sum1 = result[1];
  //   sum2 = result[2]; sum3 = result[3]; sum4 = result[4]; sum5 = result[5]; sum6 = result[6]; sum7 = result[7];
  //   sum8 = result[8]; sum9 = result[9]; sum10 = result[10]; sum11 = result[11]; sum12 = result[12];
  //   sum13 = result[13]; sum14 = result[14]; sum15 = result[15]
endmodule

module full_adder (
  input  A,
  input  B,
  input  Cin,
  output sum,
  output Cout
);

  wire A_and_B, A_and_notB, and_5_out, and_6_out, and_7_out, not_1_out, not_2_out, not_3_out, notA_and_B,
       notA_and_notB, or_1_out, or_2_out, or_3_out;

  not not_1 (not_1_out, A);
  not not_2 (not_2_out, B);
  not not_3 (not_3_out, Cin);
  or or_1 (or_1_out, notA_and_notB, A_and_B);
  or or_2 (or_2_out, notA_and_B, A_and_notB);
  or or_3 (or_3_out, notA_and_B, A_and_notB);
  and and_1 (notA_and_notB, not_1_out, not_2_out);
  and and_2 (A_and_B, A, B);
  and and_3 (notA_and_B, not_1_out, B);
  and and_4 (A_and_notB, A, not_2_out);
  and and_5 (and_5_out, or_1_out, Cin);
  and and_6 (and_6_out, not_3_out, or_2_out);
  and and_7 (and_7_out, or_3_out, Cin);
  or or_4 (Cout, and_7_out, A_and_B);
  or or_5 (sum, and_5_out, and_6_out);
endmodule
