// Logisim project cpu.circ as structural Verilog: 12 circuits, main circuit main
module main (
  input  reset
);

  wire ALUinB_chooser, and_1_out, and_2_out, and_3_out, beq, bge, branching, clk, DMwe, input_ins,
       is_greater_than, is_zero, j, jal, jr, memory_latch_1_oe_latched, memory_latch_1_we_latched, nclk,
       or_1_out, output_ins, Rdst_chooser, Rwd_chooser, Rwe, valid_data;
  wire [2:0] ALUop, multiplexer_2_out, multiplexer_3_out;
  wire [5:0] immediate;
  wire [6:0] character;
  wire [7:7] input_data;
  wire [15:0] Address, address_t, bit_extender_2_out, DataIN_memory, DataOUT_memory,
       memory_latch_1_address_latched, memory_latch_1_data_in_latched, multiplexer_1_out, multiplexer_4_out,
       multiplexer_5_out, multiplexer_6_out, multiplexer_7_out, multiplexer_8_out, multiplexer_9_out,
       next_PC, PC, PC_plus_one, PC_plus_one_plus_Branch, Rs1_val;
  wire [15:6] Instruction;

  Clock clock_1 (.out(clk));
  // Probe on {Instruction, immediate}
  TTY #(.rows(13), .cols(80)) tty_1 (.data(Rs1_val[6:0]), .clk(clk), .we(output_ins), .clr(reset));
  register_unit register_unit_1 (.result(PC), .Data(next_PC), .WE(1'b1), .reset(reset), .clk(nclk));
  // Probe on PC
  not not_1 (nclk, clk);
  assign address_t = {{4{Instruction[11]}}, {Instruction[11:6], immediate}};  // Bit_Extender bit_extender_1
  // Probe on immediate
  add_sub_unit add_sub_unit_1 (.result(PC_plus_one), .B(PC), .A(16'h1));  // open: ovf, sub
  // Probe on Instruction[8:6]
  // Probe on Instruction[11:9]
  ROM #(.addrWidth(16), .dataWidth(16)) rom_1 (.addr(PC), .data({Instruction, immediate}));
  Multiplexer #(.width(16), .enable("false")) multiplexer_1 (
    .in0(multiplexer_6_out), .in1(PC_plus_one), .out(multiplexer_1_out), .sel(jal));
  Multiplexer #(.width(3), .enable("false")) multiplexer_2 (
    .in0(Instruction[8:6]), .in1(3'b111), .out(multiplexer_2_out), .sel(jal));
  ins_decoder_and_control ins_decoder_and_control_1 (
    .Rdst_chooser(Rdst_chooser), .bge(bge), .instruction({Instruction, immediate}),
    .Rwd_chooser(Rwd_chooser), .Rwe(Rwe), .ALUop(ALUop), .DMwe(DMwe), .beq(beq),
    .ALUinB_chooser(ALUinB_chooser), .j(j), .jr(jr), .jal(jal), .input_ins(input_ins), .output_ins(output_ins));  // open: opcode
  RegisterFile registerfile_1 (
    .Rs1(Instruction[11:9]), .Rd(multiplexer_3_out), .RegWE(Rwe), .Rs2(multiplexer_2_out), .clk(clk),
    .reset(reset), .DataIn(multiplexer_1_out), .DataOut1(Rs1_val), .DataOut2(DataIN_memory));
  Multiplexer #(.width(3), .enable("false")) multiplexer_3 (
    .in0(multiplexer_2_out), .in1(immediate[5:3]), .out(multiplexer_3_out), .sel(Rdst_chooser));
  assign bit_extender_2_out = {{10{immediate[5]}}, immediate};  // Bit_Extender bit_extender_2
  Multiplexer #(.width(16), .enable("false")) multiplexer_4 (
    .in0(DataIN_memory), .in1(bit_extender_2_out), .out(multiplexer_4_out), .sel(ALUinB_chooser));
  and and_1 (and_1_out, bge, is_zero);
  ALU alu_1 (
    .result(Address), .op(ALUop), .B(multiplexer_4_out), .A(Rs1_val), .out_6(is_zero),
    .shammt(immediate[2:0]), .out_5(is_greater_than));
  and and_2 (and_2_out, beq, is_zero);
  and and_3 (and_3_out, bge, is_greater_than);
  add_sub_unit add_sub_unit_2 (
    .result(PC_plus_one_plus_Branch), .B(bit_extender_2_out), .A(PC_plus_one));  // open: ovf, sub
  or or_1 (or_1_out, and_3_out, and_1_out);
  // Probe on Address
  or or_2 (branching, and_2_out, or_1_out);
  memory_latch memory_latch_1 (
    .address(Address), .WE(DMwe), .clk(nclk), .data_in(DataIN_memory),
    .address_latched(memory_latch_1_address_latched), .WE_latched(memory_latch_1_we_latched),
    .OE_latched(memory_latch_1_oe_latched), .data_in_latched(memory_latch_1_data_in_latched));
  not not_2 (input_data[7], valid_data);
  Multiplexer #(.width(16), .enable("false")) multiplexer_5 (
    .in0(Address), .in1(DataOUT_memory), .out(multiplexer_5_out), .sel(Rwd_chooser));
  RAM #(.addrWidth(16), .dataWidth(16), .trigger("high"), .databus("bibus")) ram_1 (
    .addr(memory_latch_1_address_latched), .we(memory_latch_1_we_latched), .oe(memory_latch_1_oe_latched),
    .din(memory_latch_1_data_in_latched), .dout(DataOUT_memory));
  Multiplexer #(.width(16), .enable("false")) multiplexer_6 (
    .in0(multiplexer_5_out), .in1({{8{1'b0}}, input_data[7], character}), .out(multiplexer_6_out),
    .sel(input_ins));
  // Probe on multiplexer_6_out
  Keyboard keyboard_1 (.clk(nclk), .re(input_ins), .clr(reset), .avail(valid_data), .data(character));
  Multiplexer #(.width(16), .enable("false")) multiplexer_7 (
    .in0(PC_plus_one), .in1(PC_plus_one_plus_Branch), .out(multiplexer_7_out), .sel(branching));
  Multiplexer #(.width(16), .enable("false")) multiplexer_8 (
    .in0(multiplexer_7_out), .in1(address_t), .out(multiplexer_8_out), .sel(j));
  Multiplexer #(.width(16), .enable("false")) multiplexer_9 (
    .in0(multiplexer_8_out), .in1(Rs1_val), .out(multiplexer_9_out), .sel(jr));
  Multiplexer #(.width(16), .enable("false")) multiplexer_10 (
    .in0(multiplexer_9_out), .in1(address_t), .out(next_PC), .sel(jal));

  // Other names for the same wires on the sheet: input_data[6:0] = character; opcode[3:0] = Instruction[15:12];
  //   Instruction[5:0] = immediate; Rd[2:0] = immediate[5:3]; Rs1[2:0] = Instruction[11:9];
  //   Rs2_or_Rt[2:0] = Instruction[8:6]; shammt[2:0] = immediate[2:0]

  // Notes on the sheet:
  //   contents of rom_1 (hex, n*v repeats v):
  //   1190 5c34 5c37 d005 903f 1042 d018 1043 1141 1083 6219 a4c7 d03a 9801 b011 1140 b013 1482 b00a 9a01
  //   d018 1242 b008 903f 1dba 8c40 8c81 8cc2 8d03 8d44 8dc5 1140 5a2d 1b40 5a2d 1b40 5a29 1b40 1b47 108a
  //   d03a 191e 1912 1b7f 8b00 1640 9201 b027 1a40 d041 7c40 7c81 7cc2 7d03 7d44 7dc5 1d86 ce00 10ff 1300
  //   28a0 16c1 a83d 8a0 ce00 1dbe 8c40 8c81 0 7280 9403 f400 1241 b045 108a f400 7c40 7c81 1d82 ce00
endmodule

module full_adder (
  input  A,
  input  B,
  input  Cin,
  output sum,
  output Cout
);

  wire A_and_B, A_and_notB, and_5_out, and_6_out, and_7_out, not_1_out, not_2_out, not_3_out, notA_and_B,
       notA_and_notB, or_1_out, or_2_out, or_3_out;

  not not_1 (not_1_out, A);
  not not_2 (not_2_out, B);
  not not_3 (not_3_out, Cin);
  or or_1 (or_1_out, notA_and_notB, A_and_B);
  or or_2 (or_2_out, notA_and_B, A_and_notB);
  or or_3 (or_3_out, notA_and_B, A_and_notB);
  and and_1 (notA_and_notB, not_1_out, not_2_out);
  and and_2 (A_and_B, A, B);
  and and_3 (notA_and_B, not_1_out, B);
  and and_4 (A_and_notB, A, not_2_out);
  and and_5 (and_5_out, or_1_out, Cin);
  and and_6 (and_6_out, not_3_out, or_2_out);
  and and_7 (and_7_out, or_3_out, Cin);
  or or_4 (Cout, and_7_out, A_and_B);
  or or_5 (sum, and_5_out, and_6_out);
endmodule

module add_sub_unit (
  input  sub,
  input  [15:0] A,
  input  [15:0] B,
  output [15:0] result,
  output ovf
);

  wire Bbit0, Bbit1, Bbit2, Bbit3, Bbit4, Bbit5, Bbit6, Bbit7, Bbit8, Bbit9, Bbit10, Bbit11, Bbit12, Bbit13,
       Bbit14, Bbit15, Cout0, Cout1, Cout2, Cout3, Cout4, Cout5, Cout6, Cout7, Cout8, Cout9, Cout10, Cout11,
       Cout12, Cout13, Cout14, Cout15;

  xor xor_1 (Bbit0, B[0], sub);
  xor xor_2 (Bbit1, B[1], sub);
  xor xor_3 (Bbit2, B[2], sub);
  xor xor_4 (Bbit3, B[3], sub);
  xor xor_5 (Bbit4, B[4], sub);
  xor xor_6 (Bbit5, B[5], sub);
  xor xor_7 (Bbit6, B[6], sub);
  xor xor_8 (Bbit7, B[7], sub);
  xor xor_9 (Bbit8, B[8], sub);
  xor xor_10 (Bbit9, B[9], sub);
  xor xor_11 (Bbit10, B[10], sub);
  xor xor_12 (Bbit11, B[11], sub);
  xor xor_13 (Bbit12, B[12], sub);
  xor xor_14 (Bbit13, B[13], sub);
  xor xor_15 (Bbit14, B[14], sub);
  xor xor_16 (Bbit15, B[15], sub);
  full_adder full_adder_1 (.Cout(Cout0), .Cin(sub), .A(A[0]), .B(Bbit0), .sum(result[0]));
  full_adder full_adder_2 (.Cout(Cout1), .Cin(Cout0), .A(A[1]), .B(Bbit1), .sum(result[1]));
  full_adder full_adder_3 (.Cout(Cout2), .Cin(Cout1), .A(A[2]), .B(Bbit2), .sum(result[2]));
  full_adder full_adder_4 (.Cout(Cout3), .Cin(Cout2), .A(A[3]), .B(Bbit3), .sum(result[3]));
  full_adder full_adder_5 (.Cout(Cout4), .Cin(Cout3), .A(A[4]), .B(Bbit4), .sum(result[4]));
  full_adder full_adder_6 (.Cout(Cout5), .Cin(Cout4), .A(A[5]), .B(Bbit5), .sum(result[5]));
  full_adder full_adder_7 (.Cout(Cout6), .Cin(Cout5), .A(A[6]), .B(Bbit6), .sum(result[6]));
  full_adder full_adder_8 (.Cout(Cout7), .Cin(Cout6), .A(A[7]), .B(Bbit7), .sum(result[7]));
  full_adder full_adder_9 (.Cout(Cout8), .Cin(Cout7), .A(A[8]), .B(Bbit8), .sum(result[8]));
  full_adder full_adder_10 (.Cout(Cout9), .Cin(Cout8), .A(A[9]), .B(Bbit9), .sum(result[9]));
  full_adder full_adder_11 (.Cout(Cout10), .Cin(Cout9), .A(A[10]), .B(Bbit10), .sum(result[10]));
  full_adder full_adder_12 (.Cout(Cout11), .Cin(Cout10), .A(A[11]), .B(Bbit11), .sum(result[11]));
  full_adder full_adder_13 (.Cout(Cout12), .Cin(Cout11), .A(A[12]), .B(Bbit12), .sum(result[12]));
  full_adder full_adder_14 (.Cout(Cout13), .Cin(Cout12), .A(A[13]), .B(Bbit13), .sum(result[13]));
  full_adder full_adder_15 (.Cout(Cout14), .Cin(Cout13), .A(A[14]), .B(Bbit14), .sum(result[14]));
  full_adder full_adder_16 (.Cout(Cout15), .Cin(Cout14), .A(A[15]), .B(Bbit15), .sum(result[15]));
  xor xor_17 (ovf, Cout14, Cout15);

  // Other names for the same wires on the sheet: Abit0 = A[0]; Abit1 = A[1]; Abit2 = A[2]; Abit3 = A[3]; Abit4 = A[4];
  //   Abit5 = A[5]; Abit6 = A[6]; Abit7 = A[7]; Abit8 = A[8]; Abit9 = A[9]; Abit10 = A[10]; Abit11 = A[11];
  //   Abit12 = A[12]; Abit13 = A[13]; Abit14 = A[14]; Abit15 = A[15]; sum0 = result[0]; sum1 = result[1];
  //   sum2 = result[2]; sum3 = result[3]; sum4 = result[4]; sum5 = result[5]; sum6 = result[6]; sum7 = result[7];
  //   sum8 = result[8]; sum9 = result[9]; sum10 = result[10]; sum11 = result[11]; sum12 = result[12];
  //   sum13 = result[13]; sum14 = result[14]; sum15 = result[15]
endmodule

module nor_operation (
  input  [15:0] A,
  input  [15:0] B,
  output [15:0] result
);

  nor nor_1 (result[0], A[0], B[0]);
  nor nor_2 (result[1], A[1], B[1]);
  nor nor_3 (result[2], A[2], B[2]);
  nor nor_4 (result[3], A[3], B[3]);
  nor nor_5 (result[4], A[4], B[4]);
  nor nor_6 (result[5], A[5], B[5]);
  nor nor_7 (result[6], A[6], B[6]);
  nor nor_8 (result[7], A[7], B[7]);
  nor nor_9 (result[8], A[8], B[8]);
  nor nor_10 (result[9], A[9], B[9]);
  nor nor_11 (result[10], A[10], B[10]);
  nor nor_12 (result[11], A[11], B[11]);
  nor nor_13 (result[12], A[12], B[12]);
  nor nor_14 (result[13], A[13], B[13]);
  nor nor_15 (result[14], A[14], B[14]);
  nor nor_16 (result[15], A[15], B[15]);

  // Other names for the same wires on the sheet: Abit0 = A[0]; Abit1 = A[1]; Abit2 = A[2]; Abit3 = A[3]; Abit4 = A[4];
  //   Abit5 = A[5]; Abit6 = A[6]; Abit7 = A[7]; Abit8 = A[8]; Abit9 = A[9]; Abit10 = A[10]; Abit11 = A[11];
  //   Abit12 = A[12]; Abit13 = A[13]; Abit14 = A[14]; Abit15 = A[15]; Bbit0 = B[0]; Bbit1 = B[1]; Bbit2 = B[2];
  //   Bbit3 = B[3]; Bbit4 = B[4]; Bbit5 = B[5]; Bbit6 = B[6]; Bbit7 = B[7]; Bbit8 = B[8]; Bbit9 = B[9];
  //   Bbit10 = B[10]; Bbit11 = B[11]; Bbit12 = B[12]; Bbit13 = B[13]; Bbit14 = B[14]; Bbit15 = B[15]
endmodule

module nand_operation (
  input  [15:0] A,
  input  [15:0] B,
  output [15:0] result
);

  nand nand_1 (result[0], A[0], B[0]);
  nand nand_2 (result[1], A[1], B[1]);
  nand nand_3 (result[2], A[2], B[2]);
  nand nand_4 (result[3], A[3], B[3]);
  nand nand_5 (result[4], A[4], B[4]);
  nand nand_6 (result[5], A[5], B[5]);
  nand nand_7 (result[6], A[6], B[6]);
  nand nand_8 (result[7], A[7], B[7]);
  nand nand_9 (result[8], A[8], B[8]);
  nand nand_10 (result[9], A[9], B[9]);
  nand nand_11 (result[10], A[10], B[10]);
  nand nand_12 (result[11], A[11], B[11]);
  nand nand_13 (result[12], A[12], B[12]);
  nand nand_14 (result[13], A[13], B[13]);
  nand nand_15 (result[14], A[14], B[14]);
  nand nand_16 (result[15], A[15], B[15]);

  // Other names for the same wires on the sheet: Abit0 = A[0]; Abit1 = A[1]; Abit2 = A[2]; Abit3 = A[3]; Abit4 = A[4];
  //   Abit5 = A[5]; Abit6 = A[6]; Abit7 = A[7]; Abit8 = A[8]; Abit9 = A[9]; Abit10 = A[10]; Abit11 = A[11];
  //   Abit12 = A[12]; Abit13 = A[13]; Abit14 = A[14]; Abit15 = A[15]; Bbit0 = B[0]; Bbit1 = B[1]; Bbit2 = B[2];
  //   Bbit3 = B[3]; Bbit4 = B[4]; Bbit5 = B[5]; Bbit6 = B[6]; Bbit7 = B[7]; Bbit8 = B[8]; Bbit9 = B[9];
  //   Bbit10 = B[10]; Bbit11 = B[11]; Bbit12 = B[12]; Bbit13 = B[13]; Bbit14 = B[14]; Bbit15 = B[15]
endmodule

module left_shift (
  input  [15:0] A,
  input  [2:0] S,
  output [15:0] out_3
);

  wire byone_out0, byone_out1, byone_out2, byone_out3, byone_out4, byone_out5, byone_out6, byone_out7,
       byone_out8, byone_out9, byone_out10, byone_out11, byone_out12, byone_out13, byone_out14, byone_out15,
       bytwo_out0, bytwo_out1, bytwo_out2, bytwo_out3, bytwo_out4, bytwo_out5, bytwo_out6, bytwo_out7,
       bytwo_out8, bytwo_out9, bytwo_out10, bytwo_out11, bytwo_out12, bytwo_out13, bytwo_out14, bytwo_out15;

  Multiplexer #(.enable("false")) multiplexer_1 (.in0(A[15]), .in1(A[14]), .out(byone_out15), .sel(S[0]));
  Multiplexer #(.enable("false")) multiplexer_2 (.in0(A[14]), .in1(A[13]), .out(byone_out14), .sel(S[0]));
  Multiplexer #(.enable("false")) multiplexer_3 (.in0(A[13]), .in1(A[12]), .out(byone_out13), .sel(S[0]));
  Multiplexer #(.enable("false")) multiplexer_4 (.in0(A[12]), .in1(A[11]), .out(byone_out12), .sel(S[0]));
  Multiplexer #(.enable("false")) multiplexer_5 (.in0(A[11]), .in1(A[10]), .out(byone_out11), .sel(S[0]));
  Multiplexer #(.enable("false")) multiplexer_6 (.in0(A[10]), .in1(A[9]), .out(byone_out10), .sel(S[0]));
  Multiplexer #(.enable("false")) multiplexer_7 (.in0(A[9]), .in1(A[8]), .out(byone_out9), .sel(S[0]));
  Multiplexer #(.enable("false")) multiplexer_8 (.in0(A[8]), .in1(A[7]), .out(byone_out8), .sel(S[0]));
  Multiplexer #(.enable("false")) multiplexer_9 (.in0(A[7]), .in1(A[6]), .out(byone_out7), .sel(S[0]));
  Multiplexer #(.enable("false")) multiplexer_10 (.in0(A[6]), .in1(A[5]), .out(byone_out6), .sel(S[0]));
  Multiplexer #(.enable("false")) multiplexer_11 (.in0(A[5]), .in1(A[4]), .out(byone_out5), .sel(S[0]));
  Multiplexer #(.enable("false")) multiplexer_12 (.in0(A[4]), .in1(A[3]), .out(byone_out4), .sel(S[0]));
  Multiplexer #(.enable("false")) multiplexer_13 (.in0(A[3]), .in1(A[2]), .out(byone_out3), .sel(S[0]));
  Multiplexer #(.enable("false")) multiplexer_14 (.in0(A[2]), .in1(A[1]), .out(byone_out2), .sel(S[0]));
  Multiplexer #(.enable("false")) multiplexer_15 (.in0(A[1]), .in1(A[0]), .out(byone_out1), .sel(S[0]));
  Multiplexer #(.enable("false")) multiplexer_16 (.in0(A[0]), .in1(1'b0), .out(byone_out0), .sel(S[0]));
  Multiplexer #(.enable("false")) multiplexer_17 (.in0(byone_out15), .in1(byone_out13), .out(bytwo_out15), .sel(S[1]));
  Multiplexer #(.enable("false")) multiplexer_18 (.in0(byone_out14), .in1(byone_out12), .out(bytwo_out14), .sel(S[1]));
  Multiplexer #(.enable("false")) multiplexer_19 (.in0(byone_out13), .in1(byone_out11), .out(bytwo_out13), .sel(S[1]));
  Multiplexer #(.enable("false")) multiplexer_20 (.in0(byone_out12), .in1(byone_out10), .out(bytwo_out12), .sel(S[1]));
  Multiplexer #(.enable("false")) multiplexer_21 (.in0(byone_out11), .in1(byone_out9), .out(bytwo_out11), .sel(S[1]));
  Multiplexer #(.enable("false")) multiplexer_22 (.in0(byone_out10), .in1(byone_out8), .out(bytwo_out10), .sel(S[1]));
  Multiplexer #(.enable("false")) multiplexer_23 (.in0(byone_out9), .in1(byone_out7), .out(bytwo_out9), .sel(S[1]));
  Multiplexer #(.enable("false")) multiplexer_24 (.in0(byone_out8), .in1(byone_out6), .out(bytwo_out8), .sel(S[1]));
  Multiplexer #(.enable("false")) multiplexer_25 (.in0(byone_out7), .in1(byone_out5), .out(bytwo_out7), .sel(S[1]));
  Multiplexer #(.enable("false")) multiplexer_26 (.in0(byone_out6), .in1(byone_out4), .out(bytwo_out6), .sel(S[1]));
  Multiplexer #(.enable("false")) multiplexer_27 (.in0(byone_out5), .in1(byone_out3), .out(bytwo_out5), .sel(S[1]));
  Multiplexer #(.enable("false")) multiplexer_28 (.in0(byone_out4), .in1(byone_out2), .out(bytwo_out4), .sel(S[1]));
  Multiplexer #(.enable("false")) multiplexer_29 (.in0(byone_out3), .in1(byone_out1), .out(bytwo_out3), .sel(S[1]));
  Multiplexer #(.enable("false")) multiplexer_30 (.in0(byone_out2), .in1(byone_out0), .out(bytwo_out2), .sel(S[1]));
  Multiplexer #(.enable("false")) multiplexer_31 (.in0(byone_out1), .in1(1'b0), .out(bytwo_out1), .sel(S[1]));
  Multiplexer #(.enable("false")) multiplexer_32 (.in0(byone_out0), .in1(1'b0), .out(bytwo_out0), .sel(S[1]));
  Multiplexer #(.enable("false")) multiplexer_33 (.in0(bytwo_out15), .in1(bytwo_out11), .out(out_3[15]), .sel(S[2]));
  Multiplexer #(.enable("false")) multiplexer_34 (.in0(bytwo_out14), .in1(bytwo_out10), .out(out_3[14]), .sel(S[2]));
  Multiplexer #(.enable("false")) multiplexer_35 (.in0(bytwo_out13), .in1(bytwo_out9), .out(out_3[13]), .sel(S[2]));
  Multiplexer #(.enable("false")) multiplexer_36 (.in0(bytwo_out12), .in1(bytwo_out8), .out(out_3[12]), .sel(S[2]));
  Multiplexer #(.enable("false")) multiplexer_37 (.in0(bytwo_out11), .in1(bytwo_out7), .out(out_3[11]), .sel(S[2]));
  Multiplexer #(.enable("false")) multiplexer_38 (.in0(bytwo_out10), .in1(bytwo_out6), .out(out_3[10]), .sel(S[2]));
  Multiplexer #(.enable("false")) multiplexer_39 (.in0(bytwo_out9), .in1(bytwo_out5), .out(out_3[9]), .sel(S[2]));
  Multiplexer #(.enable("false")) multiplexer_40 (.in0(bytwo_out8), .in1(bytwo_out4), .out(out_3[8]), .sel(S[2]));
  Multiplexer #(.enable("false")) multiplexer_41 (.in0(bytwo_out7), .in1(bytwo_out3), .out(out_3[7]), .sel(S[2]));
  Multiplexer #(.enable("false")) multiplexer_42 (.in0(bytwo_out6), .in1(bytwo_out2), .out(out_3[6]), .sel(S[2]));
  Multiplexer #(.enable("false")) multiplexer_43 (.in0(bytwo_out5), .in1(bytwo_out1), .out(out_3[5]), .sel(S[2]));
  Multiplexer #(.enable("false")) multiplexer_44 (.in0(bytwo_out4), .in1(bytwo_out0), .out(out_3[4]), .sel(S[2]));
  Multiplexer #(.enable("false")) multiplexer_45 (.in0(bytwo_out3), .in1(1'b0), .out(out_3[3]), .sel(S[2]));
  Multiplexer #(.enable("false")) multiplexer_46 (.in0(bytwo_out2), .in1(1'b0), .out(out_3[2]), .sel(S[2]));
  Multiplexer #(.enable("false")) multiplexer_47 (.in0(bytwo_out1), .in1(1'b0), .out(out_3[1]), .sel(S[2]));
  Multiplexer #(.enable("false")) multiplexer_48 (.in0(bytwo_out0), .in1(1'b0), .out(out_3[0]), .sel(S[2]));

  // Other names for the same wires on the sheet: Abit0 = A[0]; Abit1 = A[1]; Abit2 = A[2]; Abit3 = A[3]; Abit4 = A[4];
  //   Abit5 = A[5]; Abit6 = A[6]; Abit7 = A[7]; Abit8 = A[8]; Abit9 = A[9]; Abit10 = A[10]; Abit11 = A[11];
  //   Abit12 = A[12]; Abit13 = A[13]; Abit14 = A[14]; Abit15 = A[15]; byfour_out0 = out_3[0]; result[15:0] = out_3;
  //   byfour_out1 = out_3[1]; byfour_out2 = out_3[2]; byfour_out3 = out_3[3]; byfour_out4 = out_3[4];
  //   byfour_out5 = out_3[5]; byfour_out6 = out_3[6]; byfour_out7 = out_3[7]; byfour_out8 = out_3[8];
  //   byfour_out9 = out_3[9]; byfour_out10 = out_3[10]; byfour_out11 = out_3[11]; byfour_out12 = out_3[12];
  //   byfour_out13 = out_3[13]; byfour_out14 = out_3[14]; byfour_out15 = out_3[15]; Sbit0 = S[0]; Sbit1 = S[1];
  //   Sbit2 = S[2]
endmodule

module ALU (
  input  [15:0] A,
  input  [15:0] B,
  input  [2:0] shammt,
  input  [2:0] op,
  output out_5,
  output out_6,
  output [15:0] result
);

  wire xor_1_out, xor_2_out, xor_3_out, xor_4_out, xor_5_out, xor_6_out, xor_7_out, xor_8_out, xor_9_out,
       xor_10_out, xor_11_out, xor_12_out, xor_13_out, xor_14_out, xor_15_out, xor_16_out;
  wire [15:0] add_result, left_shift_result, nand_result, nor_result, right_shift_result, sub_result;

  add_sub_unit add_sub_unit_1 (.result(add_result), .B(B), .A(A));  // open: ovf, sub
  add_sub_unit add_sub_unit_2 (.result(sub_result), .B(B), .A(A), .sub(1'b1));  // open: ovf
  nor_operation nor_operation_1 (.A(A), .B(B), .result(nor_result));
  nand_operation nand_operation_1 (.A(A), .B(B), .result(nand_result));
  left_shift left_shift_1 (.A(A), .S(shammt), .out_3(left_shift_result));
  right_shift right_shift_1 (.in_1(A), .in_2(shammt), .out_3(right_shift_result));
  Multiplexer #(.select(3), .width(16), .enable("false")) multiplexer_1 (
    .in0(add_result), .in1(sub_result), .in2(nor_result), .in3(nand_result), .in4(left_shift_result),
    .in5(right_shift_result), .out(result), .sel(op));  // open: in6, in7
  not not_1 (out_5, sub_result[15]);
  xor xor_1 (xor_1_out, sub_result[0], 1'b1);
  xor xor_2 (xor_2_out, sub_result[1], 1'b1);
  xor xor_3 (xor_3_out, sub_result[2], 1'b1);
  xor xor_4 (xor_4_out, sub_result[3], 1'b1);
  xor xor_5 (xor_5_out, sub_result[4], 1'b1);
  xor xor_6 (xor_6_out, sub_result[5], 1'b1);
  xor xor_7 (xor_7_out, sub_result[6], 1'b1);
  xor xor_8 (xor_8_out, sub_result[7], 1'b1);
  xor xor_9 (xor_9_out, sub_result[8], 1'b1);
  xor xor_10 (xor_10_out, sub_result[9], 1'b1);
  xor xor_11 (xor_11_out, sub_result[10], 1'b1);
  xor xor_12 (xor_12_out, sub_result[11], 1'b1);
  xor xor_13 (xor_13_out, sub_result[12], 1'b1);
  xor xor_14 (xor_14_out, sub_result[13], 1'b1);
  xor xor_15 (xor_15_out, sub_result[14], 1'b1);
  xor xor_16 (xor_16_out, sub_result[15], 1'b1);
  and and_1 (out_6, xor_1_out, xor_2_out, xor_3_out, xor_4_out, xor_5_out, xor_6_out, xor_7_out, xor_8_out, xor_9_out, xor_10_out, xor_11_out, xor_12_out, xor_13_out, xor_14_out, xor_15_out, xor_16_out);

  // Other names for the same wires on the sheet: greater_than_detector = out_5; zero_detector = out_6
endmodule

module register_unit (
  input  clk,
  input  reset,
  input  WE,
  input  [15:0] Data,
  output [15:0] result
);

  wire write;

  and and_1 (write, clk, WE);
  D_Flip_Flop d_ff_1 (.D(Data[0]), .clk(write), .Q(result[0]), .reset(reset));  // open: Qn, preset
  D_Flip_Flop d_ff_2 (.D(Data[1]), .clk(write), .Q(result[1]), .reset(reset));  // open: Qn, preset
  D_Flip_Flop d_ff_3 (.D(Data[2]), .clk(write), .Q(result[2]), .reset(reset));  // open: Qn, preset
  D_Flip_Flop d_ff_4 (.D(Data[3]), .clk(write), .Q(result[3]), .reset(reset));  // open: Qn, preset
  D_Flip_Flop d_ff_5 (.D(Data[4]), .clk(write), .Q(result[4]), .reset(reset));  // open: Qn, preset
  D_Flip_Flop d_ff_6 (.D(Data[5]), .clk(write), .Q(result[5]), .reset(reset));  // open: Qn, preset
  D_Flip_Flop d_ff_7 (.D(Data[6]), .clk(write), .Q(result[6]), .reset(reset));  // open: Qn, preset
  D_Flip_Flop d_ff_8 (.D(Data[7]), .clk(write), .Q(result[7]), .reset(reset));  // open: Qn, preset
  D_Flip_Flop d_ff_9 (.D(Data[8]), .clk(write), .Q(result[8]), .reset(reset));  // open: Qn, preset
  D_Flip_Flop d_ff_10 (.D(Data[9]), .clk(write), .Q(result[9]), .reset(reset));  // open: Qn, preset
  D_Flip_Flop d_ff_11 (.D(Data[10]), .clk(write), .Q(result[10]), .reset(reset));  // open: Qn, preset
  D_Flip_Flop d_ff_12 (.D(Data[11]), .clk(write), .Q(result[11]), .reset(reset));  // open: Qn, preset
  D_Flip_Flop d_ff_13 (.D(Data[12]), .clk(write), .Q(result[12]), .reset(reset));  // open: Qn, preset
  D_Flip_Flop d_ff_14 (.D(Data[13]), .clk(write), .Q(result[13]), .reset(reset));  // open: Qn, preset
  D_Flip_Flop d_ff_15 (.D(Data[14]), .clk(write), .Q(result[14]), .reset(reset));  // open: Qn, preset
  D_Flip_Flop d_ff_16 (.D(Data[15]), .clk(write), .Q(result[15]), .reset(reset));  // open: Qn, preset

  // Other names for the same wires on the sheet: Abit0 = Data[0]; Abit1 = Data[1]; Abit2 = Data[2]; Abit3 = Data[3];
  //   Abit4 = Data[4]; Abit5 = Data[5]; Abit6 = Data[6]; Abit7 = Data[7]; Abit8 = Data[8]; Abit9 = Data[9];
  //   Abit10 = Data[10]; Abit11 = Data[11]; Abit12 = Data[12]; Abit13 = Data[13]; Abit14 = Data[14];
  //   Abit15 = Data[15]
endmodule

module RegisterFile (
  input  [15:0] DataIn,
  input  clk,
  input  [2:0] Rd,
  input  [2:0] Rs1,
  input  [2:0] Rs2,
  input  reset,
  input  RegWE,
  output [15:0] DataOut1,
  output [15:0] DataOut2
);

  wire Enable_Rs1_0, Enable_Rs1_1, Enable_Rs1_2, Enable_Rs1_3, Enable_Rs1_4, Enable_Rs1_5, Enable_Rs1_6,
       Enable_Rs1_7, Enable_Rs2_0, Enable_Rs2_1, Enable_Rs2_2, Enable_Rs2_3, Enable_Rs2_4, Enable_Rs2_5,
       Enable_Rs2_6, Enable_Rs2_7, WE1, WE2, WE3, WE4, WE5, WE6, WE7;
  wire [15:0] Q0, Q1, Q2, Q3, Q4, Q5, Q6, Q7;

  Decoder #(.select(3)) decoder_1 (
    .out1(WE1), .out2(WE2), .out3(WE3), .out4(WE4), .out5(WE5), .out6(WE6), .out7(WE7), .sel(Rd), .en(RegWE));  // open: out0
  register_unit Reg0 (.result(Q0), .Data({16{1'b0}}), .WE(1'b0), .reset(reset), .clk(clk));
  register_unit Reg4 (.result(Q4), .Data(DataIn), .WE(WE4), .reset(reset), .clk(clk));
  // Probe on Q4
  // Probe on Q0
  Decoder #(.select(3), .enable("false")) decoder_2 (
    .out0(Enable_Rs1_0), .out1(Enable_Rs1_1), .out2(Enable_Rs1_2), .out3(Enable_Rs1_3), .out4(Enable_Rs1_4),
    .out5(Enable_Rs1_5), .out6(Enable_Rs1_6), .out7(Enable_Rs1_7), .sel(Rs1));
  register_unit Reg1 (.result(Q1), .Data(DataIn), .WE(WE1), .reset(reset), .clk(clk));
  register_unit Reg5 (.result(Q5), .Data(DataIn), .WE(WE5), .reset(reset), .clk(clk));
  // Probe on Q5
  assign DataOut1 = Enable_Rs1_0 ? Q0 : 16'bz;  // Controlled_Buffer controlled_buffer_1
  assign DataOut1 = Enable_Rs1_1 ? Q1 : 16'bz;  // Controlled_Buffer controlled_buffer_2
  assign DataOut1 = Enable_Rs1_2 ? Q2 : 16'bz;  // Controlled_Buffer controlled_buffer_3
  assign DataOut1 = Enable_Rs1_3 ? Q3 : 16'bz;  // Controlled_Buffer controlled_buffer_4
  assign DataOut1 = Enable_Rs1_4 ? Q4 : 16'bz;  // Controlled_Buffer controlled_buffer_5
  assign DataOut1 = Enable_Rs1_5 ? Q5 : 16'bz;  // Controlled_Buffer controlled_buffer_6
  assign DataOut1 = Enable_Rs1_6 ? Q6 : 16'bz;  // Controlled_Buffer controlled_buffer_7
  assign DataOut1 = Enable_Rs1_7 ? Q7 : 16'bz;  // Controlled_Buffer controlled_buffer_8
  // Probe on Q1
  Decoder #(.select(3), .enable("false")) decoder_3 (
    .out0(Enable_Rs2_0), .out1(Enable_Rs2_1), .out2(Enable_Rs2_2), .out3(Enable_Rs2_3), .out4(Enable_Rs2_4),
    .out5(Enable_Rs2_5), .out6(Enable_Rs2_6), .out7(Enable_Rs2_7), .sel(Rs2));
  register_unit Reg2 (.result(Q2), .Data(DataIn), .WE(WE2), .reset(reset), .clk(clk));
  register_unit Reg6 (.result(Q6), .Data(DataIn), .WE(WE6), .reset(reset), .clk(clk));
  // Probe on Q6
  assign DataOut2 = Enable_Rs2_0 ? Q0 : 16'bz;  // Controlled_Buffer controlled_buffer_9
  assign DataOut2 = Enable_Rs2_1 ? Q1 : 16'bz;  // Controlled_Buffer controlled_buffer_10
  assign DataOut2 = Enable_Rs2_2 ? Q2 : 16'bz;  // Controlled_Buffer controlled_buffer_11
  assign DataOut2 = Enable_Rs2_3 ? Q3 : 16'bz;  // Controlled_Buffer controlled_buffer_12
  assign DataOut2 = Enable_Rs2_4 ? Q4 : 16'bz;  // Controlled_Buffer controlled_buffer_13
  assign DataOut2 = Enable_Rs2_5 ? Q5 : 16'bz;  // Controlled_Buffer controlled_buffer_14
  assign DataOut2 = Enable_Rs2_6 ? Q6 : 16'bz;  // Controlled_Buffer controlled_buffer_15
  assign DataOut2 = Enable_Rs2_7 ? Q7 : 16'bz;  // Controlled_Buffer controlled_buffer_16
  // Probe on Q2
  register_unit Reg7 (.result(Q7), .Data(DataIn), .WE(WE7), .reset(reset), .clk(clk));
  register_unit Reg3 (.result(Q3), .Data(DataIn), .WE(WE3), .reset(reset), .clk(clk));
  // Probe on Q3
  // Probe on Q7

  // Other names for the same wires on the sheet: Data[15:0] = DataIn; Rs1Data[15:0] = DataOut1;
  //   Rs2Data[15:0] = DataOut2
endmodule

module right_shift (
  input  [15:0] in_1,
  input  [2:0] in_2,
  output [15:0] out_3
);

  wire byone_out0, byone_out1, byone_out2, byone_out3, byone_out4, byone_out5, byone_out6, byone_out7,
       byone_out8, byone_out9, byone_out10, byone_out11, byone_out12, byone_out13, byone_out14, byone_out15,
       bytwo_out0, bytwo_out1, bytwo_out2, bytwo_out3, bytwo_out4, bytwo_out5, bytwo_out6, bytwo_out7,
       bytwo_out8, bytwo_out9, bytwo_out10, bytwo_out11, bytwo_out12, bytwo_out13, bytwo_out14, bytwo_out15;

  Multiplexer #(.enable("false")) multiplexer_1 (.in0(in_1[0]), .in1(in_1[1]), .out(byone_out15), .sel(in_2[0]));
  Multiplexer #(.enable("false")) multiplexer_2 (.in0(in_1[1]), .in1(in_1[2]), .out(byone_out14), .sel(in_2[0]));
  Multiplexer #(.enable("false")) multiplexer_3 (.in0(in_1[2]), .in1(in_1[3]), .out(byone_out13), .sel(in_2[0]));
  Multiplexer #(.enable("false")) multiplexer_4 (.in0(in_1[3]), .in1(in_1[4]), .out(byone_out12), .sel(in_2[0]));
  Multiplexer #(.enable("false")) multiplexer_5 (.in0(in_1[4]), .in1(in_1[5]), .out(byone_out11), .sel(in_2[0]));
  Multiplexer #(.enable("false")) multiplexer_6 (.in0(in_1[5]), .in1(in_1[6]), .out(byone_out10), .sel(in_2[0]));
  Multiplexer #(.enable("false")) multiplexer_7 (.in0(in_1[6]), .in1(in_1[7]), .out(byone_out9), .sel(in_2[0]));
  Multiplexer #(.enable("false")) multiplexer_8 (.in0(in_1[7]), .in1(in_1[8]), .out(byone_out8), .sel(in_2[0]));
  Multiplexer #(.enable("false")) multiplexer_9 (.in0(in_1[8]), .in1(in_1[9]), .out(byone_out7), .sel(in_2[0]));
  Multiplexer #(.enable("false")) multiplexer_10 (.in0(in_1[9]), .in1(in_1[10]), .out(byone_out6), .sel(in_2[0]));
  Multiplexer #(.enable("false")) multiplexer_11 (.in0(in_1[10]), .in1(in_1[11]), .out(byone_out5), .sel(in_2[0]));
  Multiplexer #(.enable("false")) multiplexer_12 (.in0(in_1[11]), .in1(in_1[12]), .out(byone_out4), .sel(in_2[0]));
  Multiplexer #(.enable("false")) multiplexer_13 (.in0(in_1[12]), .in1(in_1[13]), .out(byone_out3), .sel(in_2[0]));
  Multiplexer #(.enable("false")) multiplexer_14 (.in0(in_1[13]), .in1(in_1[14]), .out(byone_out2), .sel(in_2[0]));
  Multiplexer #(.enable("false")) multiplexer_15 (.in0(in_1[14]), .in1(in_1[15]), .out(byone_out1), .sel(in_2[0]));
  Multiplexer #(.enable("false")) multiplexer_16 (.in0(in_1[15]), .in1(1'b0), .out(byone_out0), .sel(in_2[0]));
  Multiplexer #(.enable("false")) multiplexer_17 (
    .in0(byone_out15), .in1(byone_out13), .out(bytwo_out15), .sel(in_2[1]));
  Multiplexer #(.enable("false")) multiplexer_18 (
    .in0(byone_out14), .in1(byone_out12), .out(bytwo_out14), .sel(in_2[1]));
  Multiplexer #(.enable("false")) multiplexer_19 (
    .in0(byone_out13), .in1(byone_out11), .out(bytwo_out13), .sel(in_2[1]));
  Multiplexer #(.enable("false")) multiplexer_20 (
    .in0(byone_out12), .in1(byone_out10), .out(bytwo_out12), .sel(in_2[1]));
  Multiplexer #(.enable("false")) multiplexer_21 (
    .in0(byone_out11), .in1(byone_out9), .out(bytwo_out11), .sel(in_2[1]));
  Multiplexer #(.enable("false")) multiplexer_22 (
    .in0(byone_out10), .in1(byone_out8), .out(bytwo_out10), .sel(in_2[1]));
  Multiplexer #(.enable("false")) multiplexer_23 (.in0(byone_out9), .in1(byone_out7), .out(bytwo_out9), .sel(in_2[1]));
  Multiplexer #(.enable("false")) multiplexer_24 (.in0(byone_out8), .in1(byone_out6), .out(bytwo_out8), .sel(in_2[1]));
  Multiplexer #(.enable("false")) multiplexer_25 (.in0(byone_out7), .in1(byone_out5), .out(bytwo_out7), .sel(in_2[1]));
  Multiplexer #(.enable("false")) multiplexer_26 (.in0(byone_out6), .in1(byone_out4), .out(bytwo_out6), .sel(in_2[1]));
  Multiplexer #(.enable("false")) multiplexer_27 (.in0(byone_out5), .in1(byone_out3), .out(bytwo_out5), .sel(in_2[1]));
  Multiplexer #(.enable("false")) multiplexer_28 (.in0(byone_out4), .in1(byone_out2), .out(bytwo_out4), .sel(in_2[1]));
  Multiplexer #(.enable("false")) multiplexer_29 (.in0(byone_out3), .in1(byone_out1), .out(bytwo_out3), .sel(in_2[1]));
  Multiplexer #(.enable("false")) multiplexer_30 (.in0(byone_out2), .in1(byone_out0), .out(bytwo_out2), .sel(in_2[1]));
  Multiplexer #(.enable("false")) multiplexer_31 (.in0(byone_out1), .in1(1'b0), .out(bytwo_out1), .sel(in_2[1]));
  Multiplexer #(.enable("false")) multiplexer_32 (.in0(byone_out0), .in1(1'b0), .out(bytwo_out0), .sel(in_2[1]));
  Multiplexer #(.enable("false")) multiplexer_33 (.in0(bytwo_out15), .in1(bytwo_out11), .out(out_3[0]), .sel(in_2[2]));
  Multiplexer #(.enable("false")) multiplexer_34 (.in0(bytwo_out14), .in1(bytwo_out10), .out(out_3[1]), .sel(in_2[2]));
  Multiplexer #(.enable("false")) multiplexer_35 (.in0(bytwo_out13), .in1(bytwo_out9), .out(out_3[2]), .sel(in_2[2]));
  Multiplexer #(.enable("false")) multiplexer_36 (.in0(bytwo_out12), .in1(bytwo_out8), .out(out_3[3]), .sel(in_2[2]));
  Multiplexer #(.enable("false")) multiplexer_37 (.in0(bytwo_out11), .in1(bytwo_out7), .out(out_3[4]), .sel(in_2[2]));
  Multiplexer #(.enable("false")) multiplexer_38 (.in0(bytwo_out10), .in1(bytwo_out6), .out(out_3[5]), .sel(in_2[2]));
  Multiplexer #(.enable("false")) multiplexer_39 (.in0(bytwo_out9), .in1(bytwo_out5), .out(out_3[6]), .sel(in_2[2]));
  Multiplexer #(.enable("false")) multiplexer_40 (.in0(bytwo_out8), .in1(bytwo_out4), .out(out_3[7]), .sel(in_2[2]));
  Multiplexer #(.enable("false")) multiplexer_41 (.in0(bytwo_out7), .in1(bytwo_out3), .out(out_3[8]), .sel(in_2[2]));
  Multiplexer #(.enable("false")) multiplexer_42 (.in0(bytwo_out6), .in1(bytwo_out2), .out(out_3[9]), .sel(in_2[2]));
  Multiplexer #(.enable("false")) multiplexer_43 (.in0(bytwo_out5), .in1(bytwo_out1), .out(out_3[10]), .sel(in_2[2]));
  Multiplexer #(.enable("false")) multiplexer_44 (.in0(bytwo_out4), .in1(bytwo_out0), .out(out_3[11]), .sel(in_2[2]));
  Multiplexer #(.enable("false")) multiplexer_45 (.in0(bytwo_out3), .in1(1'b0), .out(out_3[12]), .sel(in_2[2]));
  Multiplexer #(.enable("false")) multiplexer_46 (.in0(bytwo_out2), .in1(1'b0), .out(out_3[13]), .sel(in_2[2]));
  Multiplexer #(.enable("false")) multiplexer_47 (.in0(bytwo_out1), .in1(1'b0), .out(out_3[14]), .sel(in_2[2]));
  Multiplexer #(.enable("false")) multiplexer_48 (.in0(bytwo_out0), .in1(1'b0), .out(out_3[15]), .sel(in_2[2]));

  // Other names for the same wires on the sheet: Abit15 = in_1[0]; Abit14 = in_1[1]; Abit13 = in_1[2];
  //   Abit12 = in_1[3]; Abit11 = in_1[4]; Abit10 = in_1[5]; Abit9 = in_1[6]; Abit8 = in_1[7]; Abit7 = in_1[8];
  //   Abit6 = in_1[9]; Abit5 = in_1[10]; Abit4 = in_1[11]; Abit3 = in_1[12]; Abit2 = in_1[13]; Abit1 = in_1[14];
  //   Abit0 = in_1[15]; Sbit0 = in_2[0]; Sbit1 = in_2[1]; Sbit2 = in_2[2]; byfour_out15 = out_3[0];
  //   result[15:0] = out_3; byfour_out14 = out_3[1]; byfour_out13 = out_3[2]; byfour_out12 = out_3[3];
  //   byfour_out11 = out_3[4]; byfour_out10 = out_3[5]; byfour_out9 = out_3[6]; byfour_out8 = out_3[7];
  //   byfour_out7 = out_3[8]; byfour_out6 = out_3[9]; byfour_out5 = out_3[10]; byfour_out4 = out_3[11];
  //   byfour_out3 = out_3[12]; byfour_out2 = out_3[13]; byfour_out1 = out_3[14]; byfour_out0 = out_3[15]
endmodule

module memory_latch (
  input  [15:0] address,
  input  WE,
  input  clk,
  input  [15:0] data_in,
  output [15:0] address_latched,
  output WE_latched,
  output OE_latched,
  output [15:0] data_in_latched
);

  wire DMwe_latch_q;
  wire [15:0] addr_latch_q;

  Register #(.width(16), .trigger("falling")) addr_latch (
    .D(address), .en(WE), .clk(clk), .Q(addr_latch_q));  // open: clr
  D_Flip_Flop #(.trigger("falling")) DMwe_latch (.D(WE), .clk(clk), .Q(DMwe_latch_q));  // open: Qn, preset, reset
  Register #(.width(16), .trigger("falling")) data_to_be_written (
    .D(data_in), .en(WE), .clk(clk), .Q(data_in_latched));  // open: clr
  Multiplexer #(.width(16), .enable("false")) multiplexer_1 (
    .in0(address), .in1(addr_latch_q), .out(address_latched), .sel(DMwe_latch_q));
  and and_1 (WE_latched, clk, DMwe_latch_q);
  not not_1 (OE_latched, WE_latched);
endmodule

module ins_decoder_and_control (
  input  [15:0] instruction,
  output [3:0] opcode,
  output Rwe,
  output Rdst_chooser,
  output ALUinB_chooser,
  output [2:0] ALUop,
  output Rwd_chooser,
  output DMwe,
  output beq,
  output bge,
  output j,
  output jr,
  output jal,
  output input_ins,
  output output_ins
);

  wire add, addi, nand_ins, nor_ins, shift_left, shift_right, sub;

  Decoder #(.select(4), .enable("false")) decoder_1 (
    .out0(add), .out1(addi), .out2(sub), .out3(nor_ins), .out4(nand_ins), .out5(shift_left),
    .out6(shift_right), .out7(Rwd_chooser), .out8(DMwe), .out9(beq), .out10(bge), .out11(j), .out12(jr),
    .out13(jal), .out14(input_ins), .out15(output_ins), .sel(instruction[15:12]));
  or or_1 (ALUinB_chooser, addi, Rwd_chooser, DMwe);
  or or_2 (ALUop[0], sub, nand_ins, shift_right);
  or or_3 (ALUop[1], nor_ins, nand_ins);
  or or_4 (ALUop[2], shift_left, shift_right);
  or or_5 (Rdst_chooser, add, sub, nor_ins, nand_ins, shift_left, shift_right);
  or or_6 (Rwe, add, addi, sub, nor_ins, nand_ins, shift_left, shift_right, Rwd_chooser, input_ins, jal);

  assign opcode = instruction[15:12];

  // Other names for the same wires on the sheet: bit0_ALUop = ALUop[0]; bit1_ALUop = ALUop[1]; bit2_ALUop = ALUop[2];
  //   load_word = Rwd_chooser; store_word = DMwe
endmodule
