// Logisim project recitation4.circ as structural Verilog: 2 circuits, main circuit main
module main (
);

  wire clock_1_out;
  wire [7:0] my_counter_1_q;

  Clock clock_1 (.out(clock_1_out));
  my_counter my_counter_1 (.Q(my_counter_1_q), .clk(clock_1_out));  // open: reset
  // Probe on my_counter_1_q
endmodule

module my_counter (
  input  clk,
  input  reset,
  output [7:0] Q
);

  wire [7:0] adder_1_out;

  Adder adder_1 (.a(Q), .b({8{1'b1}}), .out(adder_1_out));  // open: cin, cout
  Register register_1 (.D(adder_1_out), .clk(clk), .Q(Q), .clr(reset));  // open: en
endmodule
